# Fritzing sketch Schaltplan (saved by Fritzing 0.9.9b)

parts:
  Raspberry_Pi_4 = Raspberry Pi 4 [part_number=RPI-4-b]
  Servomotor/Schranke = Basic Servo
  LCD_Display = LCD-16X2 [package=lcd-16x2_noholes]
  RFID_Modul = RFID-RC522-v2
  Kamera = Rasberry Pi NIOR Camera [chip_label=IC package="DIP (Dual Inline) [THT]"]  # not connected

nets:
  N1: Raspberry_Pi_4.GPIO2, LCD_Display.VDD
  N2: Raspberry_Pi_4.GPIO3, LCD_Display.VO
  GND: Raspberry_Pi_4.GND, Servomotor/Schranke.gnd, LCD_Display.RS, RFID_Modul.GND
  3V3: Raspberry_Pi_4.3V3, RFID_Modul.3.3V
  N3: Raspberry_Pi_4.GPIO10, RFID_Modul.IRQ
  N4: Raspberry_Pi_4.GPIO9, RFID_Modul.MISO
  N5: Raspberry_Pi_4.GPIO11, RFID_Modul.MOSI
  N6: Raspberry_Pi_4.GPIO21, Servomotor/Schranke.pulse
  N7: Raspberry_Pi_4.GPIO8, RFID_Modul.SCK
  N8: Raspberry_Pi_4.GPIO25, RFID_Modul.RST
  5V: Raspberry_Pi_4.5V, Servomotor/Schranke.vcc, LCD_Display.VSS

custom parts:
  Raspberry Pi 4: The RPi4, a faster version of the awesome Raspberry Pi 2 B ARM Board with 40 pin gpio. Ready for special Raspberry Pi B+ and RPi2 Hat (Hardware attached (on) top)
  RFID-RC522-v2: A simple China made RFID-RC522 Reader; do check the pin labels, as this is a MFRC522 based clone.
  Rasberry Pi NIOR Camera: Camera
